# Fritzing sketch garageSwitch (saved by Fritzing 0.9.3b)
circuit board: 5.64444cm x 8.46667cm

parts:
  U3 = NodeMCU V1.0
  J2 = female pin header, 4 pins [form="♀ (female)"]
  U2 = FS1000A - 433Mhz RF Transmitter [package=THT]

nets:
  N1: U3.D4, U2.DATA
  N2: U3.D5, J2.pin1
  N3: U3.D6, J2.pin2
  GND: U3.GND, J2.pin3, U2.GND
  N4: U3.3V3, J2.pin4
  VIN: U3.Vin, U2.VCC

custom parts:
  NodeMCU V1.0: ESP8266 based NodeMCU
  FS1000A - 433Mhz RF Transmitter: This is 433Mhz RF transmitter with receiver kit for Arduino ARM MCU wireless Application environment: Remote control switch, receiver module, motorcycles, automobile anti-theft products, home security products, electric doors, shutter doors, windows, remote control socket, remote control LED, remote audio remote control electric doors, garage door remote control, remote control retractable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
