# Fritzing sketch garageSwitch2 (saved by Fritzing 0.9.3b)
breadboards: 1

parts:
  U1 = NodeMCU V1.0
  Q1 = TRANSISTOR_NPN [package=to-92-ammo]
  Relay = Screw terminal - 2 pins [package=THT]
  U2 = FS1000A - 433Mhz RF Transmitter [package=THT]
  R2 = Photocell (LDR) [package=THT]
  R1 = Resistor [tolerance=±5% resistance=220 package=THT]
  R3 = Resistor [tolerance=±5% resistance=1.2k package=THT]
  D1 = Diode [package=diode-1n4148]
  Part1 = songle relay

nets:
  N1: U1.D2, R1.Pin_1
  N2: U1.D4, U2.DATA
  3V3: U1.3V3, U1.A0, U2.VCC, R2.pin_0, R2.pin_1, R3.Pin_1
  GND: U1.GND, Q1.E, U2.GND, R3.Pin_0
  VIN: U1.Vin, D1.C, Part1.VCC
  N3: Q1.B, R1.Pin_0
  N4: Q1.C, D1.A, Part1.GND
  N5: Relay.pin1, Part1.COMMON
  N6: Relay.pin2, Part1.NO

custom parts:
  NodeMCU V1.0: ESP8266 based NodeMCU
  FS1000A - 433Mhz RF Transmitter: This is 433Mhz RF transmitter with receiver kit for Arduino ARM MCU wireless Application environment: Remote control switch, receiver module, motorcycles, automobile anti-theft products, home security products, electric doors, shutter doors, windows, remote control socket, remote control LED, remote audio remote control electric doors, garage door remote control, remote control retractable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
